// Logisim project SRAM-デコーダ.circ as structural Verilog: 1 circuit, main circuit main
module main (
  input  nSELRAM,
  input  Q0,
  input  Q1,
  input  Q2,
  input  nRD,
  input  Q3,
  input  RAM_SW,
  input  A15,
  input  nMREQ,
  input  nWR,
  input  A7,
  input  A6,
  input  A5,
  input  A4,
  input  nWR_2,
  input  nIORQ,
  output nRAMRD,
  output _8kROMRD,
  output nROMDS3,
  output nMEMCE,
  output nRAMWR,
  output CLK
);

  wire and_1_out, nand_1_out, not_1_out, or_2_out, or_4_out, or_5_out, or_7_out;

  and and_1 (and_1_out, Q0, Q1, Q2);
  and and_2 (nROMDS3, nSELRAM, RAM_SW);
  or or_1 (nMEMCE, A15, nMREQ);
  or or_2 (or_2_out, nWR_2, nIORQ);
  not not_1 (not_1_out, nROMDS3);
  or or_3 (nRAMWR, nMEMCE, nWR);
  nand nand_1 (nand_1_out, A7, A6, A5);
  or or_4 (or_4_out, nSELRAM, and_1_out, nRD);
  or or_5 (or_5_out, nRD, Q3, nROMDS3);
  or or_6 (_8kROMRD, nRD, Q3, not_1_out);
  or or_7 (or_7_out, nand_1_out, A4, or_2_out);
  not not_2 (CLK, or_7_out);
  and and_3 (nRAMRD, 1'b1, or_4_out, or_5_out);
endmodule
