// Logisim project decode1.circ as structural Verilog: 1 circuit, main circuit main
module main (
  input  nRD,
  input  nSELRAM,
  input  D0,
  input  D1,
  input  D2,
  input  D3,
  output out_7
);

  wire and_1_out, and_2_out, and_3_out, or_1_out;

  and and_1 (and_1_out, D0, D1);
  and and_2 (and_2_out, and_1_out, D2);
  or or_1 (or_1_out, nSELRAM, and_2_out);
  and and_3 (and_3_out, or_1_out, D3);
  or OUT (out_7, nRD, and_3_out);
endmodule
