// Logisim project decode2.circ as structural Verilog: 1 circuit, main circuit main
module main (
  input  nWR,
  input  nIOREQ,
  input  A4,
  input  A5,
  input  A6,
  input  A7,
  output OUT
);

  wire and_1_out, nand_1_out, or_1_out, or_2_out, or_3_out;

  or or_1 (or_1_out, nWR, nIOREQ);
  and and_1 (and_1_out, A6, A7);
  or or_2 (or_2_out, or_1_out, A4);
  nand nand_1 (nand_1_out, A5, and_1_out);
  or or_3 (or_3_out, or_2_out, nand_1_out);
  not not_1 (OUT, or_3_out);
endmodule
